# Fritzing sketch LCD Display (saved by Fritzing 0.9.6b)

parts:
  LCD1 = LCD screen
  Mod1 = Raspberry Pi 4B

nets:
  VSS: LCD1.VSS, Mod1.GND
  VDD: LCD1.VDD, Mod1.5V

notes:
  Can't find SCL or SDA
